// Logisim project Exemplo_0703.circ as structural Verilog: 1 circuit, main circuit main
module main (
  input  a,
  input  b,
  input  key,
  output s0,
  output s1
);

  wire and_1_out, and_2_out, and_3_out, and_4_out, and_5_out, nand_1_out, nor_1_out, not_1_out, or_1_out;

  not not_1 (not_1_out, key);
  and and_1 (and_1_out, b, a);
  nand nand_1 (nand_1_out, b, a);
  or or_1 (or_1_out, b, a);
  nor nor_1 (nor_1_out, a, b);
  and and_2 (and_2_out, and_1_out, not_1_out);
  and and_3 (and_3_out, key, nand_1_out);
  and and_4 (and_4_out, or_1_out, not_1_out);
  and and_5 (and_5_out, key, nor_1_out);
  or or_2 (s0, and_2_out, and_3_out);
  or or_3 (s1, and_4_out, and_5_out);
endmodule
